# Fritzing sketch p2_led_lampeggiante (saved by Fritzing 0.9.3b)
breadboards: 1

parts:
  Componente1 = Arduino Uno (Rev3)
  R1 = Resistor [tolerance=±5% resistance=220 package=THT]
  LED1 = LED - 5mm [color="Red (633nm)" package="5 mm [THT]"]

nets:
  N1: Componente1.GND, LED1.cathode
  N2: Componente1.D7, R1.Pin_1
  N3: R1.Pin_0, LED1.anode

// code stored in the sketch: p2_led_esterno.ino
// Blink Accende il led esterno 4 per 1 secondo, poi lo spegne per 1 secondo, e via cosi.

// la funzione setup parte una volta quando premi reset o dai energia alla scheda
void setup() {
  // inizializza il pin digitale 4 come output.
  pinMode(7, OUTPUT);
}
// la funzione loop function si attiva girando continuamente senza sosta
void loop() {
  digitalWrite(7, HIGH);   // accende il led (HIGH ? il massimo voltaggio)
  delay(1000);                       // attende un secondo
  digitalWrite(7, LOW);    // spegne il led dando voltaggio LOW (pari a 0)
  delay(1000);                       // attende un secondo
}
